# Fritzing sketch ArtBot (saved by Fritzing 0.9.3b)
circuit board: 2.5cm x 2.5cm
breadboards: 1

parts:
  BAT = Battery Holders [package=battcom_20mm_pth]
  U1 = NPN_PNP Transistor Array [package=sot23-6]
  85 = SO08 [chip_label=IC package=SO]
  S1 = SWITCH-MOMENTARY-2 [package=tactile-switch-1101ne]
  S2 = SWITCH-MOMENTARY-2 [package=tactile-switch-1101ne]
  PWR = smd LED [color="Red (633nm)" package="0603 [SMD]"]
  R1 = Resistor [tolerance=±5% resistance=10k package="0603 [SMD]"]
  J1 = double row female pin header, 6 pins [form="♀ (female)"]
  A = DC Motor
  Part1 = ws2812b [package="smd 2812b"]
  C = DC Motor
  B = DC Motor
  Part2 = ws2812b [package="smd 2812b"]
  Part3 = ws2812b [package="smd 2812b"]
  Q1 = NPN-Transistor [package="SOT-23 [SMD]"]
  R4 = Resistor [tolerance=±5% resistance=330 package="0603 [SMD]"]
  R5 = Resistor [tolerance=±5% resistance=330 package="0603 [SMD]"]
  Q3 = NPN-Transistor [package="SOT-23 [SMD]"]
  R6 = Resistor [tolerance=±5% resistance=330 package="0603 [SMD]"]
  Q4 = NPN-Transistor [package="SOT-23 [SMD]"]

nets:
  VDD: BAT.+, U1.C1, 85.8, PWR.cathode, R1.Pin_0, J1.pin5, A.pin_1, Part1.VDD, C.pin_1, B.pin_1, Part2.VDD, Part3.VDD
  N1: BAT.-, U1.C2, U1.B1, S1.1, S2.1
  VSS: U1.E2, 85.4, J1.pin3, Part1.VSS, Part2.VSS, Part3.VSS, Q1.1, Q3.1, Q4.1
  N2: U1.E1, S1.2, PWR.anode
  N3: 85.1, J1.pin4
  N4: 85.2, R4.Pin_0
  N5: 85.3, Part3.DIN
  N6: 85.5, S2.2, R1.Pin_1, J1.pin2
  N7: 85.6, J1.pin1, R5.Pin_0
  N8: 85.7, J1.pin6, R6.Pin_0
  N9: A.pin_2, Q1.2
  N10: Part1.DIN, Part2.DOUT
  N11: C.pin_2, Q4.2
  N12: B.pin_2, Q3.2
  N13: Part2.DIN, Part3.DOUT
  N14: Q1.0, R4.Pin_1
  N15: R5.Pin_1, Q3.0
  N16: R6.Pin_1, Q4.0

notes:
  HackBerry
  ArtBot 2.0
