# Fritzing sketch BinaryCalculator (saved by Fritzing 0.9.3b)
circuit board: 2.5cm x 2.5cm
breadboards: 1

parts:
  TINY85 = IC, DIP package, 8 pins [chip_label=IC]
  ON/OFF = female pin header, 3 pins [form="♀ (female)"]
  BAT1 = Battery Holders [package=battcom_20mm_pth]
  S1 = Momentary Switch [package=tactile-pth]
  S2 = Momentary Switch [package=tactile-pth]
  1/0 = female pin header, 3 pins [form="♀ (female)"]
  1 = LEDs [package=led-0603]
  2 = LEDs [package=led-0603]
  3 = LEDs [package=led-0603]
  4 = LEDs [package=led-0603]
  5 = LEDs [package=led-0603]
  6 = LEDs [package=led-0603]
  7 = LEDs [package=led-0603]
  8 = LEDs [package=led-0603]
  U2 = LTC6244 [package=msop8]
  U3 = LTC6244 [package=msop8]
  U4 = LTC6244 [package=msop8]

nets:
  N1: TINY85.pin2, U4.G$2_-IN
  N2: TINY85.pin3, S2.2
  N3: TINY85.pin4, BAT1.-, S1.2, S2.4, 1/0.pin3, U2.G$1_-V, U3.G$1_-V, U4.G$1_-V
  N4: TINY85.pin5, 1/0.pin2
  N5: TINY85.pin6, S1.3
  N6: TINY85.pin8, ON/OFF.pin2, ON/OFF.pin3, 1/0.pin1, 1.A, 2.A, 3.A, 4.A, 5.A, 6.A, 7.A, 8.A, U2.G$1_+V, U3.G$1_+V, U4.G$1_+V
  N7: ON/OFF.pin1, BAT1.+
  N8: 1.C, U4.G$1_OUT
  N9: 2.C, U4.G$1_-IN
  N10: 3.C, U4.G$1_+IN
  N11: 4.C, U2.G$1_OUT
  N12: 5.C, U2.G$1_-IN
  N13: 6.C, U2.G$1_+IN
  N14: 7.C, U3.G$1_OUT
  N15: 8.C, U3.G$1_-IN
  N16: U2.G$2_+IN, U3.G$2_-IN
  N17: U2.G$2_-IN, U4.G$2_+IN

notes:
  HackBerry
  Binary
  Calculator
  1.0
