# Fritzing sketch Blinky (saved by Fritzing 0.9.3b)
circuit board: 2.5cm x 2.5cm
breadboards: 1

parts:
  TINY85 = IC, DIP package, 8 pins [chip_label=IC]
  ON/OFF = female pin header, 3 pins [form="♀ (female)"]
  BAT1 = Battery Holders [package=battcom_20mm_pth]
  LED1 = LED - 5mm [color="Red (633nm)" package="5 mm [THT]"]
  LED2 = LED - 5mm [color="Red (633nm)" package="5 mm [THT]"]
  LED3 = LED - 5mm [color="Red (633nm)" package="5 mm [THT]"]
  LED4 = LED - 5mm [color="Red (633nm)" package="5 mm [THT]"]
  B = Pushbutton [package="[THT]"]
  R = Resistor [tolerance=±5% resistance=10k package=THT]

nets:
  N1: TINY85.pin2, R.Pin_1
  N2: TINY85.pin3, LED1.anode
  N3: TINY85.pin4, BAT1.-, LED1.cathode, LED2.cathode, LED3.cathode, LED4.cathode, B.Pin_1, B.Pin_2
  N4: TINY85.pin5, LED3.anode
  N5: TINY85.pin6, LED2.anode
  N6: TINY85.pin7, LED4.anode
  N7: TINY85.pin8, ON/OFF.pin2, ON/OFF.pin3
  N8: ON/OFF.pin1, BAT1.+
  N9: B.Pin_3, B.Pin_4, R.Pin_0

notes:
  HackBerry
  Blinky 1.0
