# Fritzing sketch ColorMix (saved by Fritzing 0.9.3b)
circuit board: 2.5cm x 2.5cm
breadboards: 1

parts:
  TINY85 = IC, DIP package, 8 pins [chip_label=IC]
  ON/OFF = female pin header, 3 pins [form="♀ (female)"]
  BAT1 = Battery Holders [package=battcom_20mm_pth]
  R = TRIMPOT [package=trimpot_pth_s3_lock]
  G = TRIMPOT [package=trimpot_pth_s3_lock]
  B = TRIMPOT [package=trimpot_pth_s3_lock]
  Mode = Pushbutton [package="[THT]"]
  Part1 = ws2812b [package="smd 2812b"]
  C1 = Ceramic Capacitor [capacitance=100nF package="0603 [SMD, multilayer]"]
  10K = Resistor [tolerance=±5% resistance=220 package="0603 [SMD]"]

nets:
  N1: TINY85.pin2, R.WIPER
  N2: TINY85.pin3, G.WIPER
  N3: TINY85.pin4, BAT1.-, R.CCW, G.CCW, B.CCW, Part1.VSS, C1.1, 10K.Pin_1
  N4: TINY85.pin5, B.WIPER
  N5: TINY85.pin6, Part1.DIN
  N6: TINY85.pin7, Mode.Pin_1, Mode.Pin_2, 10K.Pin_0
  N7: TINY85.pin8, ON/OFF.pin2, ON/OFF.pin3, R.CW, G.CW, B.CW, Mode.Pin_3, Mode.Pin_4, Part1.VDD, C1.0
  N8: ON/OFF.pin1, BAT1.+

notes:
  HackBerry
  Carmen 1.0
