# Fritzing sketch Compass (saved by Fritzing 0.9.3b)
circuit board: 2.5cm x 2.5cm
breadboards: 1

parts:
  BAT1 = Battery Holders [package=battcom_20mm_pth]  # not connected
  Part4 = ws2812b [package="smd 2812b"]
  Part5 = ws2812b [package="smd 2812b"]
  Part6 = ws2812b [package="smd 2812b"]
  Part7 = ws2812b [package="smd 2812b"]
  Part8 = ws2812b [package="smd 2812b"]
  Part9 = ws2812b [package="smd 2812b"]
  Part10 = ws2812b [package="smd 2812b"]
  Part11 = ws2812b [package="smd 2812b"]
  85 = SO08-EIAJ [chip_label=IC package=SO]  # not connected
  S1 = Pushbutton [package="[THT]"]  # not connected

nets:
  N1: Part4.DOUT, Part8.DIN
  N2: Part4.DIN, Part9.DOUT
  N3: Part5.DOUT, Part11.DIN
  N4: Part5.DIN, Part10.DOUT
  N5: Part6.DOUT, Part10.DIN
  N6: Part7.DOUT, Part9.DIN
  N7: Part7.DIN, Part11.DOUT

notes:
  HackBerry
  Plain 1.0
