# Fritzing sketch LEDCompass (saved by Fritzing 0.9.3b)
circuit board: 2.5cm x 2.5cm
breadboards: 1

parts:
  BAT1 = Battery Holders [package=battcom_20mm_pth]
  Part1 = ws2812b [package="smd 2812b"]
  Part2 = ws2812b [package="smd 2812b"]
  Part3 = ws2812b [package="smd 2812b"]
  Part4 = ws2812b [package="smd 2812b"]
  S2 = Pushbutton [package="[THT]"]
  S3 = Pushbutton [package="[THT]"]
  IC1 = IC, DIP package, 8 pins [chip_label=IC]
  S4 = Pushbutton [package="[THT]"]
  S5 = Pushbutton [package="[THT]"]

nets:
  VDD: BAT1.+, Part1.VDD, Part2.VDD, Part3.VDD, Part4.VDD, IC1.pin8
  VSS: BAT1.-, Part1.VSS, Part2.VSS, Part3.VSS, Part4.VSS, S2.Pin_3, S3.Pin_3, S3.Pin_4, IC1.pin4, S4.Pin_1, S5.Pin_1, S5.Pin_2
  N1: Part1.DOUT, Part3.DIN
  N2: Part1.DIN, Part2.DOUT
  N3: Part2.DIN, Part4.DOUT
  N4: Part4.DIN, IC1.pin5
  N5: S2.Pin_1, S2.Pin_2, IC1.pin3
  N6: S3.Pin_1, S3.Pin_2, IC1.pin2
  N7: IC1.pin6, S5.Pin_3, S5.Pin_4
  N8: IC1.pin7, S4.Pin_3, S4.Pin_4

notes:
  HackBerry
  Plain 1.0
