# Fritzing sketch Neo Matrix (saved by Fritzing 0.9.3b)
circuit board: 2.54cm x 2.54cm
breadboards: 1

parts:
  ON/OFF1 = female pin header, 3 pins [form="♀ (female)"]
  Part1 = ws2812b [package="smd 2812b"]
  Part2 = ws2812b [package="smd 2812b"]
  Part3 = ws2812b [package="smd 2812b"]
  Part4 = ws2812b [package="smd 2812b"]
  Part5 = ws2812b [package="smd 2812b"]
  Part6 = ws2812b [package="smd 2812b"]
  Part7 = ws2812b [package="smd 2812b"]
  Part8 = ws2812b [package="smd 2812b"]
  TINY86 = IC, DIP package, 8 pins [chip_label=IC]
  BAT2 = Battery Holders [package=battcom_20mm_pth]

nets:
  N1: ON/OFF1.pin1, BAT2.+
  VDD: ON/OFF1.pin3, Part1.VDD, Part2.VDD, Part3.VDD, Part4.VDD, Part5.VDD, Part6.VDD, Part7.VDD, Part8.VDD, TINY86.pin8
  VSS: Part1.VSS, Part8.VSS
  N2: Part1.DIN, Part2.DOUT
  VSS_2: Part2.VSS, Part3.VSS, Part4.VSS, Part5.VSS, Part6.VSS, Part7.VSS, BAT2.-
  N3: Part2.DIN, Part3.DOUT
  N4: Part3.DIN, Part7.DOUT
  N5: Part4.DOUT, Part7.DIN
  N6: Part4.DIN, Part5.DOUT
  N7: Part5.DIN, Part6.DOUT
  N8: Part6.DIN, Part8.DOUT
  N9: Part8.DIN, TINY86.pin2
