# Fritzing sketch Plain (saved by Fritzing 0.9.3b)
circuit board: 2.5cm x 2.5cm
breadboards: 1

parts:
  TINY85 = IC, DIP package, 8 pins [chip_label=IC]
  ON/OFF = female pin header, 3 pins [form="♀ (female)"]
  BAT1 = Battery Holders [package=battcom_20mm_pth]
  LED1 = LEDs [package=fkit-led-1206]
  LED2 = LEDs [package=fkit-led-1206]
  LED3 = LEDs [package=fkit-led-1206]
  LED4 = LEDs [package=fkit-led-1206]
  LED5 = LEDs [package=fkit-led-1206]
  LED6 = LEDs [package=fkit-led-1206]
  IC1 = SHIFT REGISTER [package=so16]

nets:
  N1: TINY85.pin4, BAT1.-, LED1.A, LED2.A, LED3.A, LED4.A, LED5.A, LED6.A, IC1.GND, IC1.G
  N2: TINY85.pin5, IC1.SCK
  N3: TINY85.pin6, IC1.RCK
  N4: TINY85.pin7, IC1.SER
  N5: TINY85.pin8, ON/OFF.pin2, ON/OFF.pin3, IC1.SCL, IC1.VCC
  N6: ON/OFF.pin1, BAT1.+
  N7: LED1.C, IC1.QB
  N8: LED2.C, IC1.QC
  N9: LED3.C, IC1.QD
  N10: LED4.C, IC1.QE
  N11: LED5.C, IC1.QF
  N12: LED6.C, IC1.QG

notes:
  HackBerry
  Plain 1.0
