# Fritzing sketch Programmer (saved by Fritzing 0.9.3b)
circuit board: 2.5cm x 2.5cm

parts:
  ATTiny85 = IC, DIP package, 8 pins [chip_label=IC]  # not connected
  ATTiny84 = IC, DIP package, 14 pins [chip_label=IC]
  USB = USB Connectors [package=usb-microb]
  16Mhz = Crystal [frequency="16 Mhz" package=THT]  # not connected
  R1 = Resistor [tolerance=±5% resistance=68 package="0603 [SMD]"]
  R2 = Resistor [tolerance=±5% resistance=68 package="0603 [SMD]"]
  D3 = Diode [package=sma-diode]  # not connected
  D4 = Diode [package=sma-diode]  # not connected

nets:
  N1: ATTiny84.pin1, USB.VBUS
  N2: ATTiny84.pin5, ATTiny84.pin6, R2.Pin_1
  N3: ATTiny84.pin13, R1.Pin_0
  N4: ATTiny84.pin14, USB.GND
  N5: USB.D+, R2.Pin_0
  N6: USB.D-, R1.Pin_1

notes:
  HackBerry
  Plain 1.0
