# Fritzing sketch SimonSays (saved by Fritzing 0.9.3b)
circuit board: 2.5cm x 2.5cm
breadboards: 1

parts:
  TINY85 = IC, DIP package, 8 pins [chip_label=IC]
  BAT1 = Battery Holders [package=battcom_20mm_pth]
  Part1 = ws2812b [package="smd 2812b"]
  Part2 = ws2812b [package="smd 2812b"]
  Part3 = ws2812b [package="smd 2812b"]
  Part4 = ws2812b [package="smd 2812b"]
  S1 = Pushbutton [package="[THT]"]
  S2 = Pushbutton [package="[THT]"]
  S3 = Pushbutton [package="[THT]"]
  S4 = Pushbutton [package="[THT]"]

nets:
  N1: TINY85.pin2, S4.Pin_1, S4.Pin_2
  N2: TINY85.pin3, S2.Pin_1, S2.Pin_2
  VSS: TINY85.pin4, BAT1.-, Part1.VSS, Part2.VSS, Part3.VSS, Part4.VSS, S1.Pin_1, S1.Pin_2, S2.Pin_3, S2.Pin_4, S3.Pin_3, S3.Pin_4, S4.Pin_3, S4.Pin_4
  N3: TINY85.pin5, Part4.DIN
  N4: TINY85.pin6, S3.Pin_1
  N5: TINY85.pin7, S1.Pin_3, S1.Pin_4
  VDD: TINY85.pin8, BAT1.+, Part1.VDD, Part2.VDD, Part3.VDD, Part4.VDD
  N6: Part1.DOUT, Part3.DIN
  N7: Part1.DIN, Part2.DOUT
  N8: Part2.DIN, Part4.DOUT

notes:
  HackBerry
  Simon 1.0
