# Fritzing sketch SoftLatch (saved by Fritzing 0.9.3b)
circuit board: 2.5cm x 2.5cm
breadboards: 1

parts:
  BAT = Battery Holders [package=battcom_20mm_pth]
  U1 = NPN_PNP Transistor Array [package=sot23-6]
  85 = SO08 [chip_label=IC package=SO]
  S1 = SWITCH-MOMENTARY-2 [package=tactile-switch-1101ne]
  S2 = SWITCH-MOMENTARY-2 [package=tactile-switch-1101ne]
  PWR = smd LED [color="Red (633nm)" package="0603 [SMD]"]
  R1 = Resistor [tolerance=±5% resistance=10k package="0603 [SMD]"]
  J1 = double row female pin header, 6 pins [form="♀ (female)"]

nets:
  N1: BAT.+, U1.C1, 85.8, PWR.cathode, R1.Pin_0, J1.pin5
  N2: BAT.-, U1.C2, U1.B1, S1.1, S2.1
  N3: U1.E2, 85.4, J1.pin3
  N4: U1.E1, S1.2, PWR.anode
  N5: 85.1, J1.pin4
  N6: 85.5, S2.2, R1.Pin_1, J1.pin2
  N7: 85.6, J1.pin1
  N8: 85.7, J1.pin6

notes:
  HackBerry
  Latch 1.0
